# Fritzing sketch circuits (saved by Fritzing 0.9.3b)
breadboards: 2

parts:
  LED1 = LED - 5mm [color="Red (633nm)" package="5 mm [THT]"]  # not connected
  R1 = Resistor [tolerance=±5% resistance=220 package=THT]  # not connected
  Componente1 = Arduino Uno (Rev3)  # not connected
  Componente2 = Arduino Uno (Rev3)
  LED2 = LED - 5mm [color="Red (633nm)" package="5 mm [THT]"]
  R2 = Resistor [tolerance=±5% resistance=220 package=THT]
  S1 = Pushbutton [package="[THT]"]
  R3 = Resistor [tolerance=±5% resistance=220 package=THT]

nets:
  N1: Componente2.D13/SCK, LED2.anode
  N2: Componente2.D7, R2.Pin_0, S1.Pin_1, S1.Pin_2
  N3: Componente2.5V, S1.Pin_3, S1.Pin_4
  N4: Componente2.GND, R2.Pin_1, R3.Pin_1
  N5: LED2.cathode, R3.Pin_0

notes:
  ButtonLed1, ButtonLed2
  Blink
