# Fritzing sketch circuitLedButton (saved by Fritzing 0.9.3b)
breadboards: 2

parts:
  Componente3 = Arduino Uno (Rev3)
  LED3 = LED - 5mm [color="Red (633nm)" package="5 mm [THT]"]
  R4 = Resistor [tolerance=±5% resistance=220 package=THT]
  R5 = Resistor [tolerance=±5% resistance=220 package=THT]
  S2 = Pushbutton [package="[THT]"]
  Componente4 = Arduino Uno (Rev3)
  LED4 = LED - 5mm [color="Red (633nm)" package="5 mm [THT]"]
  R7 = Resistor [tolerance=±5% resistance=220 package=THT]
  S3 = Pushbutton [package="[THT]"]
  R8 = Rotary Potentiometer (Small) [maximum_resistance=100kΩ package=THT]

nets:
  N1: Componente3.D13/SCK, LED3.anode
  N2: Componente3.D7, R5.Pin_0, S2.Pin_1, S2.Pin_2
  N3: Componente3.5V, S2.Pin_3, S2.Pin_4
  N4: Componente3.GND, R4.Pin_1, R5.Pin_1
  N5: LED3.cathode, R4.Pin_0
  N6: Componente4.D13/SCK, LED4.anode
  N7: Componente4.D7, R7.Pin_0, S3.Pin_1, S3.Pin_2
  N8: Componente4.5V, S3.Pin_3, S3.Pin_4
  N9: Componente4.GND, R7.Pin_1, R8.wiper
  N10: LED4.cathode, R8.leg2

notes:
  ButtonLed1, ButtonLed2
