# Fritzing sketch circuitLedRGB (saved by Fritzing 0.9.3b)
breadboards: 1

parts:
  Componente3 = Arduino Uno (Rev3)
  R5 = Resistor [tolerance=±5% resistance=220 package=THT]
  R6 = Resistor [tolerance=±5% resistance=220 package=THT]
  R7 = Resistor [tolerance=±5% resistance=220 package=THT]
  LED1 = RGB LED (com. cathode, rgb) [package="5 mm [THT]"]

nets:
  N1: Componente3.D9_PWM, R7.Pin_1
  N2: Componente3.D10_PWM/SS, R6.Pin_1
  N3: Componente3.D11_PWM/MOSI, R5.Pin_1
  N4: Componente3.GND, LED1.common_cathode
  N5: R5.Pin_0, LED1.blue_anode
  N6: R6.Pin_0, LED1.green_anode
  N7: R7.Pin_0, LED1.red_anode

notes:
  RGB Led
