# Fritzing sketch circuits (saved by Fritzing 0.9.3b)
breadboards: 1

parts:
  Componente2 = Arduino Uno (Rev3)
  R1 = Resistor [tolerance=±5% resistance=330 package=THT]
  D1 = Rectifier Diode [part_number=1N4001 package="300 mil [THT]"]
  M1 = DC Motor
  R2 = Photocell (LDR) [package=THT]
  R3 = Resistor [tolerance=±5% resistance=220 package=THT]
  Q1 = NPN-Transistor [package="TO92 [THT]"]

nets:
  N1: Componente2.A0, R2.pin_1, R3.Pin_0
  N2: Componente2.D3_PWM, R1.Pin_1
  N3: Componente2.5V, D1.cathode, M1.pin_1, R2.pin_0
  N4: Componente2.GND, R3.Pin_1, Q1.E
  N5: R1.Pin_0, Q1.B
  N6: D1.anode, M1.pin_2, Q1.C

notes:
  SensorUltrasomComMotor
