# Fritzing sketch circuits (saved by Fritzing 0.9.3b)
breadboards: 1

parts:
  Componente2 = Arduino Uno (Rev3)
  hc-sr2 = hc-sr04

nets:
  N1: Componente2.D6_PWM, hc-sr2.Trig
  N2: Componente2.D7, hc-sr2.Echo
  5V: Componente2.5V, hc-sr2.VCC
  GND: Componente2.GND, hc-sr2.GND

notes:
  SensorUltrasound
