# Fritzing sketch circuits (saved by Fritzing 0.9.3b)
breadboards: 1

parts:
  Componente2 = Arduino Uno (Rev3)
  J1 = Basic Force Sensing Resistor (FSR) [package=THT]
  R1 = Resistor [tolerance=±5% resistance=3.3k package=THT]

nets:
  N1: Componente2.A0, J1.pin_1, R1.Pin_0
  N2: Componente2.5V, J1.pin_0
  N3: Componente2.GND, R1.Pin_1

notes:
  Sensor Pressão
