# Fritzing sketch circuits (saved by Fritzing 0.9.3b)

parts:
  WeMos_D1_Mini_Relay_Shield_V1 = WeMos D1 Mini Relay Shield V2
  Componente2 = Arduino Uno (Rev3)
  VCC1 = 4 x AAA Battery Mount  # not connected
  M1 = DC Motor  # not connected

nets:
  3V3: WeMos_D1_Mini_Relay_Shield_V1.3V3, Componente2.3V3
  N1: WeMos_D1_Mini_Relay_Shield_V1.A0, Componente2.D2
  N2: WeMos_D1_Mini_Relay_Shield_V1.G, Componente2.GND

notes:
  Relay
